# Fritzing sketch Untitled Sketch 2 (saved by Fritzing 0.9.3b)
breadboards: 1

parts:
  Part1 = Arduino Uno (Rev3)  # not connected
  Raspberry_Pi_1 = Raspberry Pi 3 [part_number=RPI-3-V1.2]  # not connected
  LED1 = smd LED [color="Blue (525nm)" package="0603 [SMD]"]
  Part2 = Base Shield V2
  Grove2 = Grove Buzz
  Part3 = Adafruit T-Cobbler Plus [part_number="Adafruit #1989 and #2028"]
  R1 = Resistor [tolerance=±5% resistance=220 package="2010 [SMD]"]

nets:
  N1: LED1.cathode, Part3.GND
  N2: LED1.anode, R1.Pin_0
  N3: Part2.pin_140, Grove2.SIG
  N4: Part2.pin_142, Grove2.VCC
  N5: Part2.pin_143, Grove2.GND
  N6: Part3.GPIO17, R1.Pin_1

custom parts:
  Adafruit T-Cobbler Plus: The Raspberry Pi has landed on the Maker World like a 40-GPIO pinned, quad-USB ported, credit card sized bomb of DIY joy. And while you can use most of our great Model B accessories by hooking up our downgrade cable, its probably a good time to upgrade your set up and accessorize using all of the 40 pins. That's why we now carry the Assembled Adafruit Pi T-Cobbler Plus - Breakout + Cable for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
